# Fritzing sketch RC Car Internal Electronics (saved by Fritzing 0.9.10b)
breadboards: 1

parts:
  Mod1 = flyskyr6b
  Part1 = Arduino Uno (Rev3)
  J1 = Basic Servo
  M1 = BTS7960
  M2 = DC Motor [voltage_(max)=6V voltage_(min)=3V]
  U1 = LIPO-110mAh [package=lipo-110]
  VCC1 = Battery block 9V  # not connected

nets:
  N1: Mod1.CH1, J1.pulse
  N2: Mod1.CH2, Part1.D3_PWM
  VCC: Mod1.VCC, Mod1.BAT+, Part1.5V, J1.vcc, M1.pin3, M1.pin4, M1.pin7
  GND: Mod1.connector14, Mod1.GND, Part1.GND, J1.gnd, M1.pin8
  N3: Part1.D5_PWM, M1.pin1
  N4: Part1.D6_PWM, M1.pin2
  N5: M1.pin9, M2.pin_2
  N6: M1.pin10, M2.pin_1
  N7: M1.pin11, U1.+
  N8: M1.pin12, U1.-

custom parts:
  flyskyr6b: flysky r6b 6ch rc receiver module. Pcb view is 3*7 header pins, 3 female headers will let the board plug in to the receiver, or connect via wires as you choose.
  BTS7960: BTS7960 43A Peak Power H-Bridge PWM Motor Driver
